# Fritzing sketch Reciever (saved by Fritzing 0.9.10b)

parts:
  Part1 = Arduino Uno (Rev3)
  Part2 = NRF24L01+ Breakout Board
  SP1 = SPEAKER [package=pcb_mount_speaker]
  DFRobot_DFPlayer_Mini1 = DFRobot DFPlayer Mini [part_number=DFR0299]
  HC-SR501 = HC-SR501 Body Sensor Module
  KF-1 = KF-301 Relay [package=THT]

nets:
  N1: Part1.D8, Part2.CS
  N2: Part1.D9_PWM, KF-1.power
  N3: Part1.D11_PWM/MOSI, Part2.MOSI
  N4: Part1.D12/MISO, Part2.MISO
  N5: Part1.D13/SCK, Part2.SCK
  GND: Part1.GND, Part2.GND, DFRobot_DFPlayer_Mini1.GND-1, DFRobot_DFPlayer_Mini1.GND-2, HC-SR501.GND, KF-1.signal, KF-1.ground
  N6: Part1.D2, DFRobot_DFPlayer_Mini1.TX
  N7: Part1.D3_PWM, DFRobot_DFPlayer_Mini1.RX
  N8: Part1.D4, HC-SR501.OUT
  N9: Part1.D5_PWM, HC-SR501.VCC
  N10: Part1.D7, Part2.CE
  3V3: Part1.3V3, Part2.VCC
  5V: Part1.5V, DFRobot_DFPlayer_Mini1.VCC
  N11: SP1.+, KF-1.NO
  N12: SP1.-, DFRobot_DFPlayer_Mini1.SPK_1
  N13: DFRobot_DFPlayer_Mini1.SPK_2, KF-1.C

custom parts:
  HC-SR501 Body Sensor Module: Pyroelectric Infrared PIR Motion Sensor Detector Module
  KF-301 Relay: KF-301
