# Fritzing sketch Tranfer (saved by Fritzing 0.9.10b)
breadboards: 1

parts:
  Arduino_Uno = Arduino Uno (Rev3)
  part = NRF24L01+ Breakout Board
  IR1 = vs1838b [package=THT]

nets:
  N1: Arduino_Uno.D8, part.CS
  N2: Arduino_Uno.D11_PWM/MOSI, part.MOSI
  N3: Arduino_Uno.D12/MISO, part.MISO
  N4: Arduino_Uno.D13/SCK, part.SCK
  N5: Arduino_Uno.D6_PWM, IR1.Data
  N6: Arduino_Uno.D7, part.CE
  3V3: Arduino_Uno.3V3, part.VCC
  N7: Arduino_Uno.5V, IR1.Vs
  GND: Arduino_Uno.GND, part.GND, IR1.GND
